# Fritzing sketch sch (saved by Fritzing 0.9.3b)
breadboards: 1

parts:
  Part2 = Tri-Axis Gyro Breakout - L3G4200D
  USB1 = Wiring USB Adapter
  R1 = Resistor [tolerance=±5% resistance=10k package=THT]
  XTAL1 = Crystal [frequency="16 Mhz" package=SMD]
  R2 = Resistor [tolerance=±5% resistance=10k package=THT]

nets:
  GND: Part2.GND, USB1.GND
  VCC: Part2.VCC, USB1.3.3V, R1.Pin_0, R2.Pin_0
  N1: Part2.SCL, USB1.TX, R2.Pin_1
  N2: Part2.SDA, USB1.RTS, USB1.RX, R1.Pin_1
  N3: USB1.OSCI, XTAL1.pin_0
  N4: USB1.OSCO, XTAL1.pin_1

notes:
  12MHz
